# Fritzing sketch devre şeması (saved by Fritzing 0.9.4)
breadboards: 1

parts:
  Parça1 = Arduino Leonardo (Rev3b)
  S1 = Pushbutton [package="[SMD]"]
  S2 = Pushbutton [package="[SMD]"]
  S3 = Pushbutton [package="[SMD]"]
  U3 = POT_SWITCH [package=pot_pth_switch]
  U4 = POT_SWITCH [package=pot_pth_switch]
  R1 = Resistor [tolerance=±5% resistance=220 package=THT]
  R2 = Resistor [tolerance=±5% resistance=220 package=THT]
  R3 = Resistor [tolerance=±5% resistance=220 package=THT]

nets:
  N1: Parça1.D2/SDA, S1.Pin_3, S1.Pin_4, R3.Pin_0
  N2: Parça1.D3_PWM/SCL, S3.Pin_3, S3.Pin_4, R1.Pin_0
  N3: Parça1.D4/A6, S2.Pin_3, S2.Pin_4, R2.Pin_0
  N4: Parça1.5V, S2.Pin_1, S2.Pin_2, S3.Pin_1, S3.Pin_2, U3.G$1_A, U4.G$1_A
  N5: Parça1.GND, S1.Pin_1, S1.Pin_2, U3.G$2_2, U3.G$1_S, U4.G$2_2, U4.G$1_S, R1.Pin_1, R2.Pin_1, R3.Pin_1
  N6: Parça1.A0, U3.G$2_1
  N7: Parça1.A1, U4.G$2_1
